# Fritzing sketch HTU21DF-ESP32 (saved by Fritzing 0.9.3b)
breadboards: 1

parts:
  Part1 = HTU21D-F Temperature + Humidity Sensor
  Part2 = Adafruit Feather HUZZAH ESP8266 [part_number="Adafruit #2821"]
  R2 = Resistor [tolerance=±5% resistance=3.3k package=THT]
  R3 = Resistor [tolerance=±5% resistance=3.3k package=THT]

nets:
  +3V3: Part1.+3V3, Part2.3.3V, R2.Pin_1, R3.Pin_1
  GND: Part1.GND, Part2.GND
  N1: Part1.SDA, Part2.GPIO4/SDA, R3.Pin_0
  N2: Part1.SCL, Part2.GPIO5/SCL, R2.Pin_0

custom parts:
  HTU21D-F Temperature + Humidity Sensor: This I2C digital humidity sensor is an accurate and intelligent alternative to the much simpler Humidity and Temperature Sensor - SHT15 Breakout It has a typical accuracy of ±2% with an operating range that's optimized from 5% to 95% RH. Operation outside this range is still possible - just the accuracy might drop a bit. The temperature output has an accuracy of ±1°C from -30~90°C. If you're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
  Adafruit Feather HUZZAH ESP8266: his is the Adafruit Feather HUZZAH ESP8266 - our take on an 'all-in-one' ESP8266 WiFi development board with built in USB and battery charging. Its an ESP8266 WiFi module with all the extras you need, ready to rock! We have other boards in the Feather family, check'em out here. At the Feather HUZZAH's heart is an ESP8266 WiFi microcontroller clocked at 80 MHz and at 3.3V logic. This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
